# Fritzing sketch schematic (saved by Fritzing 0.9.1b)
breadboards: 1

parts:
  MV2 = MicroView [part_number=MicroView package="16pin wide"]
  Part1 = Chronodot v2.1 DS3231
  MD03A1 = Dual VNH2SP30 Motor Driver [part_number=MD03A]
  S1 = Pushbutton [package="[SMD]"]
  S2 = Pushbutton [package="[SMD]"]
  S3 = Pushbutton [package="[SMD]"]
  S4 = Pushbutton [package="[SMD]"]
  U1 = Vibration Motor- ROB-08449 [package=vibe-motor-10mm]
  U2 = LIPO-2000mAh [package=lipo-2000]
  U3 = V_REG_LD1117VXX [package=78xxl]
  Part2 = PowerBoost 500 Charger

nets:
  N1: MV2.RESET, S1.Pin_1, S1.Pin_2
  N2: MV2.A5, Part1.SCL
  N3: MV2.A4, Part1.SDA
  N4: MV2.A2, S3.Pin_1, S3.Pin_2
  N5: MV2.A1, S4.Pin_1, S4.Pin_2
  N6: MV2.A0, U2.+, Part2.VBAT
  GND: MV2.GND, S1.Pin_3, S1.Pin_4, S2.Pin_3, S2.Pin_4, S3.Pin_3, S3.Pin_4, S4.Pin_3, S4.Pin_4, U2.-, Part2.GND
  N7: MV2.RXD, MD03A1.2INb#142
  N8: MV2.TXD, MD03A1.2INb#143
  N9: MV2.D3, S2.Pin_1, S2.Pin_2
  N10: MV2.D6, MD03A1.1CS
  N11: MV2.5V, Part2.5.0V
  N12: Part1.5V, U3.IN
  GND_2: Part1.GND, MD03A1.GND, U3.GND
  N13: MD03A1.VIN, U3.OUT
  N14: MD03A1.OUT_2A, U1.-
  N15: MD03A1.OUT_2B, U1.+

custom parts:
  MicroView: MicroView - Chip-sized Arduino with OLED display.
  Chronodot v2.1 DS3231: Modified to DS3231 for naming purposes. This a custom designed module for the DS1307 Real Time Clock. The module comes fully assembled and pre-programmed with the current time (ok, so it's our current time - MST). The included Lithium coin cell battery (CR1225 41mAh) will run the module for a minimum of 9 years (17 years typical) without external 5V power. The DS1307 is accessed via the I2C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
  PowerBoost 500 Charger: The PowerBoost 500C is a little DC/DC boost converter module that can be powered by any 3.7V LiIon/LiPoly battery, and convert the battery output to 5.2V DC for running your 5V projects. At its heart is a TPS61090 boost converter from TI. This boost converter chip has some really nice extras such as low battery detection, 2A internal switch, synchronous conversion, excellent efficiency, and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
